// Logisim project ES11circuitdiagrams.circ as structural Verilog: 1 circuit, main circuit main
module main (
  input  NOT,
  input  NOT_2,
  input  in_3,
  input  AND,
  input  in_5,
  input  AND_2,
  input  in_7,
  input  OR,
  input  in_9,
  input  in_10,
  input  in_11,
  input  NAND,
  input  in_13,
  input  in_14,
  input  in_15,
  input  in_16,
  input  in_17,
  input  in_18,
  input  in_19,
  input  in_20,
  input  in_21,
  output out_22,
  output out_23,
  output out_24,
  output out_25,
  output out_26,
  output out_27,
  output out_28,
  output out_29,
  output out_30,
  output out_31,
  output out_32,
  output out_33
);

  wire nand_3_out, nand_4_out, nand_5_out, nand_6_out, nand_7_out, nand_8_out, nand_11_out, nand_12_out,
       nand_13_out, nand_14_out, nand_15_out, nand_17_out, nand_18_out, nor_2_out, nor_3_out, nor_4_out,
       nor_5_out, nor_6_out, nor_7_out, nor_10_out, nor_11_out, nor_12_out, nor_13_out, nor_16_out,
       nor_17_out, nor_18_out;

  // NAND_Gate nand_1 is placed but not wired
  nand nand_2 (out_23, NOT_2, NOT_2);
  nand nand_3 (nand_3_out, AND, in_5);
  nand nand_4 (nand_4_out, in_7, in_7);
  nand nand_5 (nand_5_out, in_9, in_9);
  nand nand_6 (nand_6_out, in_11, in_14);
  nand nand_7 (nand_7_out, in_20, in_20);
  nand nand_8 (nand_8_out, in_21, in_21);
  nand nand_9 (out_24, nand_3_out, nand_3_out);
  nand nand_10 (out_26, nand_4_out, nand_5_out);
  nand nand_11 (nand_11_out, in_11, nand_6_out);
  nand nand_12 (nand_12_out, nand_6_out, in_14);
  nand nand_13 (nand_13_out, in_16, in_16);
  nand nand_14 (nand_14_out, in_18, in_18);
  nand nand_15 (nand_15_out, in_18, in_16);
  nand nand_16 (out_29, nand_11_out, nand_12_out);
  nand nand_17 (nand_17_out, nand_13_out, nand_14_out);
  nand nand_18 (nand_18_out, nand_7_out, nand_8_out);
  nand nand_19 (out_32, nand_17_out, nand_15_out);
  nand nand_20 (out_33, nand_18_out, nand_18_out);
  nor nor_1 (out_22, NOT, NOT);
  nor nor_2 (nor_2_out, in_3, in_3);
  nor nor_3 (nor_3_out, AND_2, AND_2);
  nor nor_4 (nor_4_out, OR, OR);
  nor nor_5 (nor_5_out, in_10, in_10);
  nor nor_6 (nor_6_out, NAND, NAND);
  nor nor_7 (nor_7_out, in_13, in_15);
  nor nor_8 (out_25, nor_2_out, nor_3_out);
  nor nor_9 (out_27, nor_4_out, nor_4_out);
  nor nor_10 (nor_10_out, nor_5_out, nor_6_out);
  nor nor_11 (nor_11_out, in_13, nor_7_out);
  nor nor_12 (nor_12_out, nor_7_out, in_15);
  nor nor_13 (nor_13_out, in_17, in_19);
  nor nor_14 (out_28, nor_10_out, nor_10_out);
  nor nor_15 (out_30, nor_11_out, nor_12_out);
  nor nor_16 (nor_16_out, in_17, nor_13_out);
  nor nor_17 (nor_17_out, nor_13_out, in_19);
  nor nor_18 (nor_18_out, nor_16_out, nor_17_out);
  nor nor_19 (out_31, nor_18_out, nor_18_out);

  // Notes on the sheet:
  //   OR
  //   XOR
  //   XNOR
  //   NOR
  //   XNOR
  //   XOR
endmodule
