// Logisim project hroac2ES11.circ as structural Verilog: 1 circuit, main circuit main
module main (
  input  A,
  input  B,
  input  Cin,
  input  A_2,
  input  B_2,
  input  Cin_2,
  input  A_3,
  input  B_3,
  input  A0,
  input  B0,
  input  A1,
  input  B1,
  output LA,
  output LB,
  output Sum,
  output LA_2,
  output LB_2,
  output Cout,
  output LD,
  output LB_3,
  output LC,
  output LA_3,
  output LC_2,
  output LB_4,
  output LA_4
);

  wire G2_2_out, G2_4_out, G3_2_out, G3_out, G4_2_out, G4_4_out, not_1_out, not_2_out;

  xor G1 (LA, A, B);
  and G2 (LB, A, B);
  xor G3 (G3_out, A_3, B_3);
  and G4 (LA_3, A_3, B_3);
  xor G1_2 (LC_2, A0, B0);
  and G2_2 (G2_2_out, A0, B0);
  xor G3_2 (G3_2_out, A1, B1);
  nand G4_2 (G4_2_out, A1, B1);
  xor G1_3 (LA_2, A_2, B_2);
  and G2_3 (LB_2, A_2, B_2);
  and G4_3 (LB_3, Cin_2, G3_out);
  xor G1_4 (Sum, Cin, LA_2);
  and G2_4 (G2_4_out, Cin, LA_2);
  xor G3_3 (LB_4, G2_2_out, G3_2_out);
  nand G4_4 (G4_4_out, G2_2_out, G3_2_out);
  or or_1 (Cout, G2_4_out, LB_2);
  xor G3_4 (LD, Cin_2, G3_out);
  or G4_5 (LC, LB_3, LA_3);
  not not_1 (not_1_out, G4_4_out);
  not not_2 (not_2_out, G4_2_out);
  or G4_6 (LA_4, not_1_out, not_2_out);

  // Notes on the sheet:
  //   SW2
  //   SW3
  //   SW1
  //   SW2
  //   SW3
  //   SW3
  //   SW3
  //   SW2
  //   SW3
  //   SW2
  //   SW2
  //   S
  //   Co
  //   sum
  //   Cout
  //   S0
  //   S1
  //   Cout
endmodule
